// Logisim project 2400040454-11-.circ as structural Verilog: 1 circuit, main circuit main
module main (
  input  A,
  input  [3:0] in_2,
  input  B,
  input  [3:0] in_4,
  input  C,
  input  [3:0] in_6,
  input  D,
  input  [3:0] in_8,
  output [3:0] out_9,
  output out_10,
  output COFFEE,
  output [3:0] out_12,
  output out_13,
  output TEA,
  output out_15,
  output [3:0] out_16,
  output MILK,
  output out_18,
  output [3:0] out_19,
  output HOT_WATER
);

  wire clock_1_out, comparator_1_eq, comparator_2_eq, comparator_3_eq, comparator_4_eq, not_1_out, not_2_out,
       not_3_out, not_4_out;

  not not_1 (not_1_out, B);
  not not_2 (not_2_out, A);
  not not_3 (not_3_out, C);
  not not_4 (not_4_out, D);
  and and_1 (out_10, A, not_1_out, not_3_out, not_4_out);
  and and_2 (out_13, B, not_2_out, not_3_out, not_4_out);
  and and_3 (out_15, C, not_2_out, not_1_out, not_4_out);
  and and_4 (out_18, D, not_2_out, not_1_out, not_3_out);
  Clock clock_1 (.out(clock_1_out));
  Counter #(.width(4), .max('hf)) counter_1 (.Q(out_9), .clk(clock_1_out));  // open: load, D, count, carry, clr
  Counter #(.width(4), .max('hf)) counter_2 (.Q(out_12), .clk(clock_1_out));  // open: load, D, count, carry, clr
  Counter #(.width(4), .max('hf)) counter_3 (.Q(out_16), .clk(clock_1_out));  // open: load, D, count, carry, clr
  Counter #(.width(4), .max('hf)) counter_4 (.Q(out_19), .clk(clock_1_out));  // open: load, D, count, carry, clr
  Comparator #(.width(4)) comparator_1 (.a(out_9), .b(in_2), .eq(comparator_1_eq));  // open: gt, lt
  Comparator #(.width(4)) comparator_2 (.a(out_12), .b(in_4), .eq(comparator_2_eq));  // open: gt, lt
  Comparator #(.width(4)) comparator_3 (.a(out_16), .b(in_6), .eq(comparator_3_eq));  // open: gt, lt
  Comparator #(.width(4)) comparator_4 (.a(out_19), .b(in_8), .eq(comparator_4_eq));  // open: gt, lt
  and and_5 (COFFEE, out_10, comparator_1_eq);
  and and_6 (TEA, out_13, comparator_2_eq);
  and and_7 (MILK, out_15, comparator_3_eq);
  and and_8 (HOT_WATER, out_18, comparator_4_eq);

  // Notes on the sheet:
  //   VENDING MACHINE
endmodule
