// Logisim project 2400040454_1..circ as structural Verilog: 1 circuit, main circuit main
module main (
  input  A,
  input  B,
  input  B_2,
  input  C,
  input  A_2,
  input  B_3,
  output out_7
);

  wire or_1_out, or_2_out;

  or or_1 (or_1_out, A, B);
  or or_2 (or_2_out, B_2, C);
  // OR_Gate or_3 has open pins: in1=A_2, in3=B_3, out=open
  and and_1 (out_7, or_1_out, or_2_out);

  // Notes on the sheet:
  //   (A+B).(B+C)
endmodule
