// Logisim project 2400040454_10_.circ as structural Verilog: 1 circuit, main circuit main
module main (
  input  [3:0] Input,
  input  [3:0] Input_2,
  input  [3:0] Input_3,
  input  [1:0] Select_line,
  input  [1:0] Select_line_2,
  input  [3:0] Input_4,
  output [3:0] Output,
  output [3:0] Output_2,
  output [3:0] Output_3,
  output [3:0] Output_4,
  output [3:0] Output_5,
  output [3:0] Output_6,
  output [3:0] Output_7,
  output [3:0] Output_8
);

  wire Clock_out;
  wire [3:0] demultiplexer_1_out0, demultiplexer_1_out1, demultiplexer_1_out2, demultiplexer_1_out3,
       multiplexer_1_out;

  Clock Clock (.out(Clock_out));
  Register #(.width(4)) Register (.D(Input), .Q(Output), .clk(Clock_out));  // open: en, clr
  Register #(.width(4)) Register_2 (.D(Input_2), .Q(Output_3), .clk(Clock_out));  // open: en, clr
  Register #(.width(4)) Register_3 (.D(Input_3), .Q(Output_5), .clk(Clock_out));  // open: en, clr
  Register #(.width(4)) Register_4 (.D(Input_4), .Q(Output_7), .clk(Clock_out));  // open: en, clr
  Multiplexer #(.select(2), .width(4)) multiplexer_1 (
    .in0(Output), .in1(Output_3), .in2(Output_5), .in3(Output_7), .out(multiplexer_1_out), .sel(Select_line));  // open: en
  Demultiplexer #(.select(2), .width(4)) demultiplexer_1 (
    .out0(demultiplexer_1_out0), .out1(demultiplexer_1_out1), .out2(demultiplexer_1_out2),
    .out3(demultiplexer_1_out3), .in(multiplexer_1_out), .sel(Select_line_2));  // open: en
  Register #(.width(4)) Register_5 (.D(demultiplexer_1_out0), .Q(Output_2), .clk(Clock_out));  // open: en, clr
  Register #(.width(4)) Register_6 (.D(demultiplexer_1_out1), .Q(Output_4), .clk(Clock_out));  // open: en, clr
  Register #(.width(4)) Register_7 (.D(demultiplexer_1_out2), .Q(Output_6), .clk(Clock_out));  // open: en, clr
  Register #(.width(4)) Register_8 (.D(demultiplexer_1_out3), .Q(Output_8), .clk(Clock_out));  // open: en, clr
endmodule
