// Logisim project 2400040454_2_.circ as structural Verilog: 1 circuit, main circuit main
module main (
  input  A,
  input  B,
  input  A_2,
  input  A_3,
  input  B_2,
  input  A_4,
  input  B_3,
  input  A_5,
  input  A_6,
  input  A_7,
  input  B_4,
  input  B_5,
  input  A_8,
  input  B_6,
  output out_15,
  output out_16,
  output out_17,
  output out_18,
  output out_19,
  output out_20,
  output out_21,
  output out_22
);

  wire nand_3_out, nand_4_out, nand_5_out, nand_6_out, nand_10_out, nand_11_out, nand_12_out, nand_13_out,
       nand_14_out, nand_15_out, nand_16_out, nand_17_out, nand_19_out, nand_20_out;

  nand nand_1 (out_15, A, A, B);
  nand nand_2 (out_16, A_2, A_2);
  nand nand_3 (nand_3_out, A_4, B_3);
  nand nand_4 (nand_4_out, A_6, A_6);
  nand nand_5 (nand_5_out, A_7, A_7);
  nand nand_6 (nand_6_out, B_5, B_5);
  not nand_7 (out_18, nand_3_out);  // NAND_Gate
  not nand_8 (out_19, nand_4_out);  // NAND_Gate
  nand nand_9 (out_21, nand_5_out, nand_6_out);
  nand nand_10 (nand_10_out, A_3, B_2, B_2);
  nand nand_11 (nand_11_out, nand_10_out, nand_10_out);
  nand nand_12 (nand_12_out, nand_10_out, B_2, B_2);
  nand nand_13 (nand_13_out, A_5, A_5, A_5);
  nand nand_14 (nand_14_out, B_4, B_4);
  nand nand_15 (nand_15_out, A_8, B_6, B_6);
  nand nand_16 (nand_16_out, A_8, A_8);
  nand nand_17 (nand_17_out, B_6, B_6, B_6);
  nand nand_18 (out_17, nand_11_out, nand_12_out);
  not nand_19 (nand_19_out, nand_13_out);  // NAND_Gate
  nand nand_20 (nand_20_out, nand_16_out, nand_17_out, nand_17_out);
  not nand_21 (out_20, nand_19_out);  // NAND_Gate
  nand nand_22 (out_22, nand_15_out, nand_20_out);
endmodule
