// Logisim project 2400040454_3_.circ as structural Verilog: 1 circuit, main circuit main
module main (
  input  KEY,
  input  carDoor,
  input  seat_belt,
  output buzzer
);

  wire and_1_out, and_2_out, and_3_out, not_1_out, not_2_out;

  not not_1 (not_1_out, carDoor);
  not not_2 (not_2_out, seat_belt);
  and and_1 (and_1_out, KEY, carDoor, seat_belt);
  LED led_1 (.in(and_1_out));
  LED Engine (.in(and_1_out));
  and and_2 (and_2_out, KEY, not_1_out);
  and and_3 (and_3_out, KEY, not_2_out);
  or or_1 (buzzer, and_2_out, and_3_out);
endmodule
