// Logisim project 2400040454_4_.circ as structural Verilog: 1 circuit, main circuit main
module main (
  input  D0,
  input  S0,
  input  S1,
  input  D1,
  input  D2,
  input  D3,
  input  in_7,
  input  [1:0] in_8,
  input  D3_2,
  input  D2_2,
  input  D1_2,
  input  D0_2
);

  wire and_1_out, and_2_out, and_3_out, and_4_out, multiplexer_1_out, not_1_out, not_2_out, or_1_out;

  not not_1 (not_1_out, S0);
  not not_2 (not_2_out, S1);
  and and_1 (and_1_out, D3_2, S0, S1);
  and and_2 (and_2_out, D2_2, S0, not_2_out);
  and and_3 (and_3_out, D1_2, not_1_out, S1);
  and and_4 (and_4_out, D0_2, not_1_out, not_2_out);
  Multiplexer #(.select(2)) multiplexer_1 (
    .in0(D0), .in1(D1), .in2(D2), .in3(D3), .out(multiplexer_1_out), .sel(in_8), .en(in_7));
  LED led_1 (.in(multiplexer_1_out));
  or or_1 (or_1_out, and_1_out, and_2_out, and_3_out, and_4_out);
  LED led_2 (.in(or_1_out));

  // Notes on the sheet:
  //   !S0
  //   !S1
endmodule
