// Logisim project 2400040454_6_.circ as structural Verilog: 1 circuit, main circuit main
// km
module main (
  input  [3:0] A,
  input  [3:0] B,
  input  [1:0] select_lines,
  input  Enable,
  output [3:0] RESULT
);

  wire [3:0] AND_out, NOR_out, XNOR_2_out, XNOR_out;

  assign AND_out = B & A;  // AND_Gate AND, 4 bits wide
  assign NOR_out = ~(B | A);  // NOR_Gate NOR, 4 bits wide
  assign XNOR_out = ~(B ^ A);  // XNOR_Gate XNOR, 4 bits wide
  assign XNOR_2_out = ~(B ^ A);  // XNOR_Gate XNOR_2, 4 bits wide
  Multiplexer #(.select(2), .width(4)) multiplexer_1 (
    .in0(AND_out), .in1(NOR_out), .in2(XNOR_out), .in3(XNOR_2_out), .out(RESULT), .sel(select_lines),
    .en(Enable));
endmodule
