// Logisim project 2400040454_7_.circ as structural Verilog: 1 circuit, main circuit main
module main (
  input  in_1,
  input  in_2,
  input  in_3,
  input  in_4
);

  wire clock_out, D_Flipflop_2_q, D_Flipflop_3_q, D_Flipflop_4_q, D_Flipflop_q, undriven, XOR_Gate_out;

  Clock clock (.out(clock_out));
  D_Flip_Flop D_Flipflop (
    .clk(clock_out), .D(D_Flipflop_4_q), .Q(D_Flipflop_q), .en(undriven));  // open: Qn, preset, reset
  LED LED_1 (.in(D_Flipflop_q));
  xor XOR_Gate (XOR_Gate_out, D_Flipflop_q, D_Flipflop_4_q);
  D_Flip_Flop D_Flipflop_2 (
    .clk(clock_out), .D(XOR_Gate_out), .Q(D_Flipflop_2_q), .en(in_1));  // open: Qn, preset, reset
  LED LED_2 (.in(D_Flipflop_2_q));
  D_Flip_Flop D_Flipflop_3 (
    .clk(clock_out), .D(D_Flipflop_2_q), .Q(D_Flipflop_3_q), .en(in_2));  // open: Qn, preset, reset
  LED LED_3 (.in(D_Flipflop_3_q));
  D_Flip_Flop D_Flipflop_4 (
    .clk(clock_out), .D(D_Flipflop_3_q), .Q(D_Flipflop_4_q), .en(in_3));  // open: Qn, preset, reset
  LED LED_4 (.in(D_Flipflop_4_q));
endmodule
