// Logisim project 2400040454_8_.circ as structural Verilog: 1 circuit, main circuit main
module main (
  input  INPUT
);

  wire AND_out, CLOCK_out, Dflipflop_2_q, Dflipflop_3_q, Dflipflop_4_q, Dflipflop_q, NOT_2_out, NOT_out;

  Clock CLOCK (.out(CLOCK_out));
  D_Flip_Flop Dflipflop (.clk(CLOCK_out), .D(INPUT), .Q(Dflipflop_q));  // open: Qn, preset, en, reset
  not NOT (NOT_out, Dflipflop_q);
  D_Flip_Flop Dflipflop_2 (.clk(CLOCK_out), .D(Dflipflop_q), .Q(Dflipflop_2_q));  // open: Qn, preset, en, reset
  D_Flip_Flop Dflipflop_3 (.clk(CLOCK_out), .D(Dflipflop_2_q), .Q(Dflipflop_3_q));  // open: Qn, preset, en, reset
  not NOT_2 (NOT_2_out, Dflipflop_3_q);
  D_Flip_Flop Dflipflop_4 (.clk(CLOCK_out), .D(Dflipflop_3_q), .Q(Dflipflop_4_q));  // open: Qn, preset, en, reset
  LED OUTPUT (.in(AND_out));
  and AND (AND_out, Dflipflop_4_q, NOT_2_out, Dflipflop_2_q, NOT_out);
endmodule
