// Logisim project 2400040454_9_.circ as structural Verilog: 1 circuit, main circuit main
module main (
  output out_1,
  output out_2,
  output out_3,
  output out_4,
  output out_5,
  output out_6,
  output out_7,
  output out_8
);

  wire clock_1_out, clock_2_out, d_ff_1_qn, d_ff_2_qn, d_ff_3_qn, d_ff_4_qn, d_ff_5_qn, d_ff_6_qn, d_ff_7_qn,
       d_ff_8_qn;

  Clock clock_1 (.out(clock_1_out));
  Clock clock_2 (.out(clock_2_out));
  D_Flip_Flop d_ff_1 (.clk(clock_1_out), .D(d_ff_1_qn), .Q(out_1), .Qn(d_ff_1_qn));  // open: preset, en, reset
  D_Flip_Flop d_ff_2 (.clk(clock_2_out), .D(d_ff_2_qn), .Q(out_5), .Qn(d_ff_2_qn));  // open: preset, en, reset
  D_Flip_Flop d_ff_3 (.clk(out_1), .D(d_ff_3_qn), .Q(out_2), .Qn(d_ff_3_qn));  // open: preset, en, reset
  D_Flip_Flop d_ff_4 (.clk(d_ff_2_qn), .D(d_ff_4_qn), .Q(out_6), .Qn(d_ff_4_qn));  // open: preset, en, reset
  D_Flip_Flop d_ff_5 (.clk(out_2), .D(d_ff_5_qn), .Q(out_3), .Qn(d_ff_5_qn));  // open: preset, en, reset
  D_Flip_Flop d_ff_6 (.clk(d_ff_4_qn), .D(d_ff_6_qn), .Q(out_7), .Qn(d_ff_6_qn));  // open: preset, en, reset
  D_Flip_Flop d_ff_7 (.clk(out_3), .D(d_ff_7_qn), .Q(out_4), .Qn(d_ff_7_qn));  // open: preset, en, reset
  D_Flip_Flop d_ff_8 (.clk(d_ff_6_qn), .D(d_ff_8_qn), .Q(out_8), .Qn(d_ff_8_qn));  // open: preset, en, reset
endmodule
